// Digital circuit Decoder.dig as structural Verilog
module Decoder (
  input  [7:0] Instruction,
  output [3:0] Operand,
  output Input_reg,
  output Output_reg
);


  assign Input_reg = Instruction[5];
  assign Operand = Instruction[3:0];
  assign Output_reg = Instruction[4];

  // Notes on the sheet:
  //   Instruction: default 15
endmodule
