// Digital circuit Encoder.dig as structural Verilog
module Encoder (
  input  [3:0] Operand,
  input  Output_reg,
  input  Input_reg,
  output [7:0] Instruction
);


  assign Instruction = {2'b00, Input_reg, Output_reg, Operand};

  // Notes on the sheet:
  //   Operand: default 15
endmodule
