// Digital circuit Main.dig as structural Verilog
module Main (
  input  [3:0] in_4,
  input  in_5,
  input  in_6,
  input  [3:0] in_7,
  input  in_8,
  input  in_9,
  output [3:0] R0,
  output [3:0] out_2,
  output [3:0] R1
);

  wire button_1_out, counter_1_out, decoder_1_input_reg, decoder_1_output_reg;
  wire [3:0] add_1_s, decoder_1_operand;
  wire [7:0] encoder_1_instruction, encoder_2_instruction, multiplexer_1_out;

  Encoder encoder_1 (.Operand(in_4), .Output_reg(in_5), .Input_reg(in_6), .Instruction(encoder_1_instruction));
  Encoder encoder_2 (.Operand(in_7), .Output_reg(in_8), .Input_reg(in_9), .Instruction(encoder_2_instruction));
  Button button_1 (.out(button_1_out));
  Counter counter_1 (.en(1'b1), .C(button_1_out), .clr(1'b0), .out(counter_1_out));  // open: ovf
  Multiplexer #(.Bits(8)) multiplexer_1 (
    .sel(counter_1_out), .in_0(encoder_1_instruction), .in_1(encoder_2_instruction), .out(multiplexer_1_out));
  Decoder decoder_1 (
    .Instruction(multiplexer_1_out), .Operand(decoder_1_operand), .Input_reg(decoder_1_input_reg),
    .Output_reg(decoder_1_output_reg));
  Add #(.Bits(4)) add_1 (.a(decoder_1_operand), .b(out_2), .c_i(1'b0), .s(add_1_s));  // open: c_o
  RegisterFile registerfile_1 (
    .Input(add_1_s), .Input_reg(decoder_1_input_reg), .Output_reg(decoder_1_output_reg),
    .Clock(button_1_out), .Output(out_2), .R0(R0), .R1(R1));

  // Notes on the sheet:
  //   in_4: default 1
  //   in_9: default 1
endmodule
