// Digital circuit RegisterFile.dig as structural Verilog
module RegisterFile (
  input  [3:0] Input,
  input  Input_reg,
  input  Output_reg,
  input  Clock,
  output [3:0] Output,
  output [3:0] R0,
  output [3:0] R1
);

  wire decoder_1_out_0, decoder_1_out_1;
  wire [3:0] demultiplexer_1_out_0, demultiplexer_1_out_1;

  Demultiplexer #(.Bits(4)) demultiplexer_1 (
    .sel(Input_reg), .in(Input), .out_0(demultiplexer_1_out_0), .out_1(demultiplexer_1_out_1));
  Decoder decoder_1 (.sel(Input_reg), .out_0(decoder_1_out_0), .out_1(decoder_1_out_1));
  Register #(.Bits(4)) register_1 (.D(demultiplexer_1_out_0), .C(Clock), .en(decoder_1_out_0), .Q(R0));
  Register #(.Bits(4)) register_2 (.D(demultiplexer_1_out_1), .C(Clock), .en(decoder_1_out_1), .Q(R1));
  Multiplexer #(.Bits(4)) multiplexer_1 (.sel(Output_reg), .in_0(R0), .in_1(R1), .out(Output));

  // Notes on the sheet:
  //   Input: default 6
endmodule
